# Fritzing sketch scheme (saved by Fritzing 1.0.2b)

parts:
  WeMos_D1_Mini1 = WeMos D1 Mini
  U1 = SWITCH_SPDT [package=kps-1290]
  LED2 = RGB LED (com. cathode, rgb) [color="Red (633nm)" current=0.030A package="5 mm [THT]"]
  R2 = Resistor [tolerance=±5% resistance=220 package="2010 [SMD]"]
  R3 = Resistor [tolerance=±5% resistance=220 package="2010 [SMD]"]
  J1 = Piezo Speaker
  R1 = Resistor [tolerance=±5% resistance=220 package="2010 [SMD]"]
  J2 = Piezo Speaker
  R4 = Resistor [tolerance=±5% power=0.25W resistance=330000 package=THT]

nets:
  N1: WeMos_D1_Mini1.3V3, U1.O, U1.P
  N2: WeMos_D1_Mini1.D0, U1.S, R4.Pin_1
  N3: WeMos_D1_Mini1.D1, R1.Pin_0
  N4: WeMos_D1_Mini1.D2, R3.Pin_0
  N5: WeMos_D1_Mini1.D5, J1.pin2
  N6: WeMos_D1_Mini1.D7, R2.Pin_0
  N7: WeMos_D1_Mini1.D8, J2.pin2
  N8: WeMos_D1_Mini1.G, LED2.common_cathode, J1.pin1, J2.pin1, R4.Pin_0
  N9: LED2.red_anode, R1.Pin_1
  N10: LED2.green_anode, R3.Pin_1
  N11: LED2.blue_anode, R2.Pin_1
